# Fritzing sketch huang_dan (saved by Fritzing 0.9.2b)
circuit board: 8.46667cm x 5.64444cm
breadboards: 1

parts:
  LCD1 = LCD screen
  J1 = Piezo Speaker  # not connected
  LED1 = LED - 5mm [color="Red (633nm)" package="5 mm [THT]"]  # not connected
  LED2 = LED - 5mm [color="Red (633nm)" package="5 mm [THT]"]
  LED3 = RGB LED (com. cathode, rgb) [package="5 mm [THT]"]  # not connected
  VCC1 = Battery  # not connected
  元件1 = Arduino Uno (Rev3)
  microSD_Transflash1 = SparkFun - microSD Transflash
  R1 = Resistor [tolerance=±5% resistance=220 package=THT]
  R3 = Resistor [tolerance=±5% resistance=220 package=THT]
  R4 = Rotary Potentiometer (Small) [maximum_resistance=100kΩ package=THT]
  S1 = Pushbutton [package="[THT]"]  # not connected
  S2 = Pushbutton [package="[THT]"]  # not connected
  Power_RGB1 = Prolight RGB 3 Watt Star  # not connected
  7_Segment1 = 7 Segment Display  # not connected
  Matrix_keypad2 = KEYPAD 4x4  # not connected
  U2 = 74HC595 [package="DIP16 [THT]"]  # not connected
  U4 = 74HC595 [package="DIP16 [THT]"]
  C1 = Ceramic Capacitor [capacitance=100nF package="100 mil [THT, multilayer]"]  # not connected
  C2 = Ceramic Capacitor [capacitance=100nF package="100 mil [THT, multilayer]"]  # not connected

nets:
  GND: LCD1.VSS, LCD1.R/W, 元件1.GND, microSD_Transflash1.GND, R1.Pin_0, R3.Pin_1, U4.GND, U4.OE
  VCC: LCD1.VDD, LCD1.LED+, 元件1.5V, microSD_Transflash1.VCC, R4.leg1, U4.MR, U4.VCC
  N1: LCD1.V0, R4.wiper
  N2: LCD1.RS, U4.Q1
  N3: LCD1.E, U4.Q3
  N4: LCD1.DB4, U4.Q4
  N5: LCD1.DB5, U4.Q5
  N6: LCD1.DB6, U4.Q6
  N7: LCD1.DB7, U4.Q7
  N8: LCD1.LED-, R1.Pin_1
  N9: LED2.cathode, 元件1.D3_PWM
  N10: LED2.anode, R3.Pin_0
  N11: 元件1.D10_PWM/SS, microSD_Transflash1.DO
  N12: 元件1.D11_PWM/MOSI, microSD_Transflash1.SCK
  N13: 元件1.D12/MISO, microSD_Transflash1.DI
  N14: 元件1.D13/SCK, microSD_Transflash1.CS
  N15: 元件1.D4, U4.DS
  N16: 元件1.D5_PWM, U4.ST_CP
  N17: 元件1.D6_PWM, U4.SH_CP

custom parts:
  KEYPAD 4x4: Matrix keypad 16 buttons, 4 rows x 4 columns
